// Digital circuit 2023CPU16.dig as structural Verilog
module _2023CPU16 (
  input  [15:0] ROM_INSTR,
  input  [15:0] ROM_IMM,
  input  CLK_CPU,
  output [15:0] ROM_ADDR,
  output [15:0] ROM_IMM_ADDR,
  output [15:0] PORTA,
  output [15:0] PORTB,
  output [15:0] GPR_AIO
);

  wire and_1_out, and_2_out, and_3_out, and_4_out, and_5_out, and_6_out, and_7_out, and_8_out, and_9_out,
       bitselector_1_out, comparator_1_eq, comparator_2_lt, comparator_3_eq, comparator_4_eq, counter_1_ovf,
       F_C, F_N, F_V, F_Z, lookuptable_1_out, MODE_ALU, MODE_BRANCH, MODE_MEM, multiplexer_5_out,
       multiplexer_6_out, not_1_out, not_2_out, not_3_out, not_4_out, not_5_out, or_1_out, or_2_out, PHASE_0,
       PHASE_1, PHASE_2, PHASE_3, xnor_1_out;
  wire [1:0] counter_1_out;
  wire [3:0] alu_1_r_n;
  wire [7:4] FLAGS;
  wire [15:0] add_1_s, add_3_s, alu_1_r, GPR_B, IMM, INSTR, iomem_1_rvalue, iomem_1_sp, multiplexer_1_out,
       multiplexer_2_out, multiplexer_3_out, multiplexer_4_out, multiplexer_7_out, multiplexer_8_out,
       multiplexer_9_out, multiplexer_10_out, multiplexer_11_out, ramdualport_1_d;
  wire [15:8] iomem_1_flags;

  BitSelector #(.Selector_Bits(3)) bitselector_1 (
    .in({FLAGS, F_V, F_N, F_Z, F_C}), .sel(INSTR[6:4]), .out(bitselector_1_out));
  xnor xnor_1 (xnor_1_out, bitselector_1_out, INSTR[7]);
  or or_1 (or_1_out, ~INSTR[8], xnor_1_out);  // Or
  and and_1 (and_1_out, MODE_BRANCH, or_1_out);
  Counter #(.Bits(2)) counter_1 (.en(1'b1), .C(CLK_CPU), .clr(counter_1_ovf), .out(counter_1_out), .ovf(counter_1_ovf));
  Decoder #(.Selector_Bits(2)) decoder_1 (
    .sel(counter_1_out), .out_0(PHASE_0), .out_1(PHASE_1), .out_2(PHASE_2), .out_3(PHASE_3));
  Register #(.Bits(16)) u_INSTR (.D(ROM_INSTR), .C(CLK_CPU), .en(PHASE_0), .Q(INSTR));
  Register #(.Bits(16)) u_IMM (.D(ROM_IMM), .C(CLK_CPU), .en(PHASE_0), .Q(IMM));
  Comparator #(.Bits(4)) comparator_1 (.a(INSTR[12:9]), .b(4'b0000), .eq(comparator_1_eq));  // open: gt, lt
  Multiplexer #(.Bits(16)) multiplexer_1 (
    .sel(and_1_out), .in_0(add_1_s), .in_1(multiplexer_2_out), .out(multiplexer_1_out));
  and and_2 (and_2_out, comparator_1_eq, MODE_BRANCH);
  Multiplexer #(.Bits(16)) multiplexer_2 (.sel(and_2_out), .in_0(GPR_AIO), .in_1(IMM), .out(multiplexer_2_out));
  Register #(.Bits(16)) IP (.D(multiplexer_1_out), .C(CLK_CPU), .en(PHASE_2), .Q(ROM_ADDR));
  or or_2 (or_2_out, and_2_out, and_3_out, comparator_4_eq);
  and and_3 (and_3_out, INSTR[12], MODE_MEM);
  LookUpTable lookuptable_1 (.in0(MODE_ALU), .in1(MODE_MEM), .out(lookuptable_1_out));
  Multiplexer #(.Bits(16)) multiplexer_3 (.sel(or_2_out), .in_0({16{1'b0}}), .in_1(16'h1), .out(multiplexer_3_out));
  Add #(.Bits(16)) add_1 (.a(ROM_ADDR), .b(multiplexer_3_out), .c_i(1'b1), .s(add_1_s));  // open: c_o
  Add #(.Bits(16)) add_2 (.a(ROM_ADDR), .b({16{1'b0}}), .c_i(1'b1), .s(ROM_IMM_ADDR));  // open: c_o
  Decoder #(.Selector_Bits(2)) decoder_2 (
    .sel(INSTR[15:14]), .out_0(MODE_ALU), .out_1(MODE_MEM), .out_2(MODE_BRANCH));  // open: out_3
  and and_4 (and_4_out, PHASE_2, not_1_out);
  not not_1 (not_1_out, INSTR[8]);
  Multiplexer #(.Bits(16)) multiplexer_4 (
    .sel(lookuptable_1_out), .in_0(alu_1_r), .in_1(multiplexer_11_out), .out(multiplexer_4_out));
  Multiplexer multiplexer_5 (.sel(lookuptable_1_out), .in_0(PHASE_2), .in_1(and_4_out), .out(multiplexer_5_out));
  Multiplexer multiplexer_6 (.sel(not_2_out), .in_0(PHASE_2), .in_1(PHASE_1), .out(multiplexer_6_out));
  and and_5 (and_5_out, multiplexer_5_out, ~MODE_BRANCH);  // And
  and and_6 (and_6_out, MODE_ALU, PHASE_2);
  and and_7 (and_7_out, multiplexer_6_out, MODE_MEM, comparator_3_eq);
  RegisterFile #(.AddrBits(4), .Bits(16)) GPRs (
    .Din(multiplexer_4_out), .we(and_5_out), .Rw(INSTR[3:0]), .C(CLK_CPU), .Ra(INSTR[3:0]), .Rb(INSTR[7:4]),
    .Da(GPR_AIO), .Db(GPR_B));
  Multiplexer #(.Bits(16)) multiplexer_7 (
    .sel(comparator_3_eq), .in_0(multiplexer_8_out), .in_1(iomem_1_sp), .out(multiplexer_7_out));
  Multiplexer #(.Bits(16)) multiplexer_8 (.sel(not_3_out), .in_0(IMM), .in_1(GPR_B), .out(multiplexer_8_out));
  ALU alu_1 (
    .A(GPR_AIO), .B(GPR_B), .OP(INSTR[12:9]), .C_en(INSTR[8]), .C_in(F_C), .R(alu_1_r), .R_N(alu_1_r_n[2]),
    .R_C(alu_1_r_n[0]), .R_V(alu_1_r_n[3]), .R_Z(alu_1_r_n[1]));
  Comparator #(.Bits(16)) comparator_2 (.a(multiplexer_7_out), .b(16'h20), .lt(comparator_2_lt));  // open: gt, eq
  not not_2 (not_2_out, INSTR[8]);
  not not_3 (not_3_out, INSTR[12]);
  not not_4 (not_4_out, comparator_2_lt);
  and and_8 (and_8_out, not_4_out, INSTR[8]);
  not not_5 (not_5_out, and_8_out);
  Comparator #(.Bits(4)) comparator_3 (.a(4'b0100), .b(INSTR[12:9]), .eq(comparator_3_eq));  // open: gt, lt
  and and_9 (and_9_out, INSTR[8], comparator_2_lt);
  RAMDualPort #(.AddrBits(16), .Bits(16)) ramdualport_1 (
    .A(multiplexer_7_out), .Din(GPR_AIO), .str(and_8_out), .C(CLK_CPU), .ld(not_5_out), .D(ramdualport_1_d));
  IOMEM iomem_1 (
    .WADDR(multiplexer_7_out[4:0]), .WVALUE(GPR_AIO), .FLAGSIN({{8{1'b0}}, FLAGS, alu_1_r_n}),
    .W_EN(and_9_out), .FLAGSW_EN(and_6_out), .CLK(CLK_CPU), .RADDR(multiplexer_7_out[4:0]),
    .SPW_EN(and_7_out), .SPIN(add_3_s), .SP(iomem_1_sp), .FLAGS({iomem_1_flags, FLAGS, F_V, F_N, F_Z, F_C}),
    .RVALUE(iomem_1_rvalue), .PORTA(PORTA), .PORTB(PORTB));  // open: PINA, PINB, TRX, TTX, PULSE
  Add #(.Bits(16)) add_3 (.a(iomem_1_sp), .b(multiplexer_9_out), .c_i(1'b0), .s(add_3_s));  // open: c_o
  Multiplexer #(.Bits(16)) multiplexer_9 (.sel(INSTR[8]), .in_0(16'h1), .in_1({16{1'b1}}), .out(multiplexer_9_out));
  Multiplexer #(.Bits(16)) multiplexer_10 (
    .sel(comparator_2_lt), .in_0(ramdualport_1_d), .in_1(iomem_1_rvalue), .out(multiplexer_10_out));
  Multiplexer #(.Bits(16)) multiplexer_11 (
    .sel(comparator_4_eq), .in_0(multiplexer_10_out), .in_1(IMM), .out(multiplexer_11_out));
  Comparator #(.Bits(3)) comparator_4 (.a(INSTR[11:9]), .b(3'b110), .eq(comparator_4_eq));  // open: gt, lt

  // Other names for the same wires on the sheet: FLAGS[3:0] = {F_V, F_N, F_Z, F_C}; GPR_A[15:0] = GPR_AIO

  // Notes on the sheet:
  //   contents of lookuptable_1 (hex, n*v repeats v):
  //   0,a,1
endmodule
