// Digital circuit IOMEM.dig as structural Verilog
module IOMEM (
  input  [4:0] WADDR,
  input  [15:0] WVALUE,
  input  [15:0] FLAGSIN,
  input  W_EN,
  input  FLAGSW_EN,
  input  CLK,
  input  [4:0] RADDR,
  input  SPW_EN,
  input  [15:0] SPIN,
  input  [15:0] PINA,
  input  [15:0] PINB,
  input  [15:0] TRX,
  output [15:0] SP,
  output [15:0] FLAGS,
  output [15:0] RVALUE,
  output [15:0] PORTA,
  output [15:0] PORTB,
  output [15:0] TTX,
  output [15:0] PULSE
);

  wire decoder_1_out_1, decoder_1_out_2, decoder_1_out_3, decoder_1_out_4, decoder_1_out_7, decoder_1_out_9,
       or_1_out, or_2_out;
  wire [4:0] driver_1_out;
  wire [15:0] multiplexer_1_out, multiplexer_2_out, multiplexer_3_out, PINA_q, PINB_q, TRX_q;

  Multiplexer #(.Bits(16)) multiplexer_1 (.sel(SPW_EN), .in_0(WVALUE), .in_1(SPIN), .out(multiplexer_1_out));
  or or_1 (or_1_out, SPW_EN, decoder_1_out_1);
  assign driver_1_out = W_EN ? WADDR : 5'bz;  // Driver driver_1
  assign driver_1_out = ~W_EN ? {5{1'b0}} : 5'bz;  // DriverInvSel driverinvsel_1
  Decoder #(.Selector_Bits(5)) decoder_1 (
    .sel(driver_1_out), .out_1(decoder_1_out_1), .out_2(decoder_1_out_2), .out_3(decoder_1_out_3),
    .out_4(decoder_1_out_4), .out_7(decoder_1_out_7), .out_9(decoder_1_out_9));  // open: out_0, out_5, out_6, out_8, out_10, out_11, out_12, out_13, out_14, out_15, out_16, out_17, out_18, out_19, out_20, out_21, out_22, out_23, out_24, out_25, out_26, out_27, out_28, out_29, out_30, out_31
  Register #(.Bits(16)) u_SP (.D(multiplexer_1_out), .C(CLK), .en(or_1_out), .Q(SP));
  or or_2 (or_2_out, FLAGSW_EN, decoder_1_out_2);
  Multiplexer #(.Bits(16)) multiplexer_2 (.sel(FLAGSW_EN), .in_0(WVALUE), .in_1(FLAGSIN), .out(multiplexer_2_out));
  Register #(.Bits(16)) u_FLAGS (.D(multiplexer_2_out), .C(CLK), .en(or_2_out), .Q(FLAGS));
  Register #(.Bits(16)) u_PORTA (.D(WVALUE), .C(CLK), .en(decoder_1_out_3), .Q(PORTA));
  Register #(.Bits(16)) u_PORTB (.D(WVALUE), .C(CLK), .en(decoder_1_out_4), .Q(PORTB));
  Register #(.Bits(16)) u_PINA (.D(PINA), .C(CLK), .en(1'b1), .Q(PINA_q));
  Register #(.Bits(16)) u_PINB (.D(PINB), .C(CLK), .en(1'b1), .Q(PINB_q));
  Register #(.Bits(16)) u_TTX (.D(WVALUE), .C(CLK), .en(decoder_1_out_7), .Q(TTX));
  Register #(.Bits(16)) u_TRX (.D(TRX), .C(CLK), .en(1'b1), .Q(TRX_q));
  Register #(.Bits(16)) u_PULSE (.D(multiplexer_3_out), .C(CLK), .en(1'b1), .Q(PULSE));
  Multiplexer #(.Bits(16)) multiplexer_3 (
    .sel(decoder_1_out_9), .in_0({16{1'b0}}), .in_1(WVALUE), .out(multiplexer_3_out));
  Multiplexer #(.Selector_Bits(5), .Bits(16)) multiplexer_4 (
    .sel(RADDR), .in_0({16{1'b0}}), .in_1(SP), .in_2(FLAGS), .in_3(PORTA), .in_4(PORTB), .in_5(PINA_q),
    .in_6(PINB_q), .in_7(TTX), .in_8(TRX_q), .in_9(PULSE), .in_10({16{1'b0}}), .in_11({16{1'b0}}),
    .in_12({16{1'b0}}), .in_13({16{1'b0}}), .in_14({16{1'b0}}), .in_15({16{1'b0}}), .in_16({16{1'b0}}),
    .in_17({16{1'b0}}), .in_18({16{1'b0}}), .in_19({16{1'b0}}), .in_20({16{1'b0}}), .in_21({16{1'b0}}),
    .in_22({16{1'b0}}), .in_23({16{1'b0}}), .in_24({16{1'b0}}), .in_25({16{1'b0}}), .in_26({16{1'b0}}),
    .in_27({16{1'b0}}), .in_28({16{1'b0}}), .in_29({16{1'b0}}), .in_30({16{1'b0}}), .in_31({16{1'b0}}),
    .out(RVALUE));
endmodule
